// Logisim project CPU.circ as structural Verilog: 6 circuits, main circuit CPU
module CPU (
);

  wire alu_1_less_than, and_1_out, clock_1_out, control_unit_1_alusearch, control_unit_1_branch,
       control_unit_1_call, control_unit_1_halt, control_unit_1_jump, control_unit_1_memread,
       control_unit_1_memtoreg, control_unit_1_memwrite, control_unit_1_min, control_unit_1_regdst,
       control_unit_1_regwrite, control_unit_1_rightshift, control_unit_1_rtn, control_unit_1_zero,
       not_1_out, or_1_out, or_2_out;
  wire [2:0] alu_control_1_operation, control_unit_1_aluop, multiplexer_3_out, multiplexer_4_out;
  wire [4:0] rom_1_data;
  wire [15:0] adder_1_out, adder_2_out, additional_alu_1_out_4, alu_1_aluoutput, bit_extender_1_out,
       bit_extender_2_out, multiplexer_1_out, multiplexer_2_out, multiplexer_5_out, multiplexer_6_out,
       ram_1_data, register_1_q, register_2_q, register_file_1_read_data_1, register_file_1_read_data_2;
  wire [15:5] rom_1_data_2;

  Adder #(.width(16)) adder_1 (.a(adder_2_out), .b(16'h1), .out(adder_1_out));  // open: cin, cout
  Register #(.width(16)) register_1 (
    .D(multiplexer_1_out), .en(not_1_out), .Q(register_1_q), .clk(clock_1_out));  // open: clr
  not not_1 (not_1_out, control_unit_1_halt);
  Clock clock_1 (.out(clock_1_out));
  Multiplexer #(.width(16), .enable("false")) multiplexer_1 (
    .in0(multiplexer_2_out), .in1(register_2_q), .out(multiplexer_1_out), .sel(control_unit_1_rtn));
  Register #(.width(16)) register_2 (
    .D(adder_1_out), .en(control_unit_1_call), .Q(register_2_q), .clk(control_unit_1_call));  // open: clr
  and and_1 (and_1_out, control_unit_1_branch, alu_1_less_than);
  Additional_ALU additional_alu_1 (
    .in_1(register_1_q), .in_3(bit_extender_1_out), .negative(rom_1_data_2[5]), .out_4(additional_alu_1_out_4));
  Adder #(.width(16)) adder_2 (.a(16'h1), .b(register_1_q), .out(adder_2_out));  // open: cin, cout
  or or_1 (or_1_out, control_unit_1_jump, and_1_out);
  Multiplexer #(.width(16), .enable("false")) multiplexer_2 (
    .in0(adder_2_out), .in1(additional_alu_1_out_4), .out(multiplexer_2_out), .sel(or_1_out));
  ROM #(.addrWidth(16), .dataWidth(16)) rom_1 (.addr(register_1_q), .data({rom_1_data_2, rom_1_data}));  // open: sel
  assign bit_extender_1_out = {{11{1'b0}}, rom_1_data};  // Bit_Extender bit_extender_1
  Control_Unit control_unit_1 (
    .opcode(rom_1_data_2[15:12]), .jump(control_unit_1_jump), .RegDst(control_unit_1_regdst),
    .RegWrite(control_unit_1_regwrite), .aluSearch(control_unit_1_alusearch),
    .MemWrite(control_unit_1_memwrite), .AluOP(control_unit_1_aluop), .zero(control_unit_1_zero),
    .min(control_unit_1_min), .rightShift(control_unit_1_rightshift), .call(control_unit_1_call),
    .halt(control_unit_1_halt), .branch(control_unit_1_branch), .MemRead(control_unit_1_memread),
    .MemToReg(control_unit_1_memtoreg), .rtn(control_unit_1_rtn));
  Multiplexer #(.width(3), .enable("false")) multiplexer_3 (
    .in0(rom_1_data_2[8:6]), .in1({rom_1_data_2[5], rom_1_data[4:3]}), .out(multiplexer_3_out),
    .sel(control_unit_1_regdst));
  assign bit_extender_2_out = {{10{1'b0}}, {rom_1_data_2[5], rom_1_data}};  // Bit_Extender bit_extender_2
  Register_File register_file_1 (
    .read_reg_1(rom_1_data_2[11:9]), .read_reg_2(rom_1_data_2[8:6]), .write_data(multiplexer_6_out),
    .read_data_1(register_file_1_read_data_1), .read_data_2(register_file_1_read_data_2),
    .write_reg(multiplexer_3_out), .Halt(control_unit_1_halt), .clk(clock_1_out),
    .writeEn(control_unit_1_regwrite));
  Multiplexer #(.width(3), .enable("false")) multiplexer_4 (
    .in0(rom_1_data[2:0]), .in1(3'b000), .out(multiplexer_4_out), .sel(control_unit_1_alusearch));
  Multiplexer #(.width(16), .enable("false")) multiplexer_5 (
    .in0(register_file_1_read_data_2), .in1(bit_extender_2_out), .out(multiplexer_5_out),
    .sel(control_unit_1_alusearch));
  ALU_control alu_control_1 (
    .func(multiplexer_4_out), .ALUop(control_unit_1_aluop), .Operation(alu_control_1_operation));
  ALU alu_1 (
    .Operand1(register_file_1_read_data_1), .Operand2(multiplexer_5_out), .ALUOutput(alu_1_aluoutput),
    .in_1(alu_control_1_operation), .less_than(alu_1_less_than), .zero(control_unit_1_zero),
    .min(control_unit_1_min), .shiftRight(control_unit_1_rightshift));
  or or_2 (or_2_out, control_unit_1_memwrite, control_unit_1_memread);
  RAM #(.addrWidth(16), .dataWidth(16), .bus("separate")) ram_1 (
    .addr(register_file_1_read_data_1), .din(alu_1_aluoutput), .data(ram_1_data),
    .str(control_unit_1_memwrite), .sel(or_2_out), .clk(clock_1_out), .ld(control_unit_1_memread));  // open: clr
  Multiplexer #(.width(16), .enable("false")) multiplexer_6 (
    .in0(alu_1_aluoutput), .in1(ram_1_data), .out(multiplexer_6_out), .sel(control_unit_1_memtoreg));

  // Notes on the sheet:
  //   change
  //   inst
  //   contents of rom_1 (hex, n*v repeats v):
  //   5006 5044 6007 7098 5007 5048 6003 70a0 c003 50 8000 f000
  //   opcode
endmodule

module ALU (
  input  [2:0] in_1,
  input  [15:0] Operand1,
  input  [15:0] Operand2,
  input  zero,
  input  min,
  input  shiftRight,
  output [15:0] ALUOutput,
  output less_than
);

  wire comparator_1_gt, multiplexer_4_out;
  wire [15:0] adder_1_out, and_1_out, multiplexer_1_out, multiplexer_2_out, multiplexer_3_out,
       multiplier_1_out, negator_1_out, or_1_out, shifter_1_out, shifter_2_out, shifter_3_out, zero_q;

  Register #(.width(16)) u_zero (.en(zero), .Q(zero_q));  // open: D, clk, clr
  Multiplexer #(.width(16), .enable("false")) multiplexer_1 (
    .in0(Operand1), .in1(zero_q), .out(multiplexer_1_out), .sel(zero));
  Shifter #(.width(16)) shifter_1 (.in(multiplexer_1_out), .\dist (Operand2[3:0]), .out(shifter_1_out));
  Shifter #(.width(16), .shift("lr")) shifter_2 (.in(multiplexer_1_out), .\dist (Operand2[3:0]), .out(shifter_2_out));
  Shifter #(.width(16), .shift("ar")) shifter_3 (.in(multiplexer_1_out), .\dist (Operand2[3:0]), .out(shifter_3_out));
  Adder #(.width(16)) adder_1 (.a(multiplexer_1_out), .b(Operand2), .out(adder_1_out));  // open: cin, cout
  Multiplier #(.width(16)) multiplier_1 (
    .a(multiplexer_1_out), .b(Operand2), .out(multiplier_1_out));  // open: cin, cout
  Negator #(.width(16)) negator_1 (.in(multiplexer_1_out), .out(negator_1_out));
  assign and_1_out = multiplexer_1_out & Operand2;  // AND_Gate and_1, 16 bits wide
  assign or_1_out = multiplexer_1_out | Operand2;  // OR_Gate or_1, 16 bits wide
  Comparator #(.width(16), .mode("unsigned")) comparator_1 (
    .a(multiplexer_1_out), .b(Operand2), .gt(comparator_1_gt), .lt(less_than));  // open: eq
  Multiplexer #(.width(16), .enable("false")) multiplexer_2 (
    .in0(shifter_1_out), .in1(shifter_2_out), .out(multiplexer_2_out), .sel(shiftRight));
  Multiplexer #(.width(16), .enable("false")) multiplexer_3 (
    .in0(Operand2), .in1(multiplexer_1_out), .out(multiplexer_3_out), .sel(multiplexer_4_out));
  Multiplexer #(.enable("false")) multiplexer_4 (
    .in0(comparator_1_gt), .in1(less_than), .out(multiplexer_4_out), .sel(min));
  Multiplexer #(.select(3), .width(16), .enable("false")) multiplexer_5 (
    .in0(adder_1_out), .in1(multiplier_1_out), .in2(negator_1_out), .in3(and_1_out), .in4(or_1_out),
    .in5(multiplexer_3_out), .in6(multiplexer_2_out), .in7(shifter_3_out), .out(ALUOutput), .sel(in_1));

  // Notes on the sheet:
  //   max
endmodule

module Register_File (
  input  Halt,
  input  [2:0] read_reg_1,
  input  [2:0] read_reg_2,
  input  [2:0] write_reg,
  input  [15:0] write_data,
  input  writeEn,
  input  clk,
  output [15:0] read_data_1,
  output [15:0] read_data_2
);

  wire and_1_out, and_2_out, and_3_out, and_4_out, and_5_out, and_6_out, and_7_out, and_8_out,
       decoder_1_out0, decoder_1_out1, decoder_1_out2, decoder_1_out3, decoder_1_out4, decoder_1_out5,
       decoder_1_out6, decoder_1_out7, not_1_out;
  wire [15:0] r1_q, r2_q, r3_q, r4_q, r5_q, r6_q, r7_q, r8_q;

  Decoder #(.select(3)) decoder_1 (
    .out0(decoder_1_out0), .out1(decoder_1_out1), .out2(decoder_1_out2), .out3(decoder_1_out3),
    .out4(decoder_1_out4), .out5(decoder_1_out5), .out6(decoder_1_out6), .out7(decoder_1_out7),
    .sel(write_reg), .en(not_1_out));
  not not_1 (not_1_out, Halt);
  and and_1 (and_1_out, decoder_1_out0, writeEn);
  and and_2 (and_2_out, decoder_1_out1, writeEn);
  and and_3 (and_3_out, decoder_1_out2, writeEn);
  and and_4 (and_4_out, decoder_1_out3, writeEn);
  and and_5 (and_5_out, decoder_1_out4, writeEn);
  and and_6 (and_6_out, decoder_1_out5, writeEn);
  and and_7 (and_7_out, decoder_1_out6, writeEn);
  and and_8 (and_8_out, decoder_1_out7, writeEn);
  Register #(.width(16)) r1 (.D(write_data), .en(and_1_out), .Q(r1_q), .clk(clk), .clr(1'b0));
  Register #(.width(16)) r2 (.D(write_data), .en(and_2_out), .Q(r2_q), .clk(clk), .clr(1'b0));
  Register #(.width(16)) r3 (.D(write_data), .en(and_3_out), .Q(r3_q), .clk(clk), .clr(1'b0));
  Register #(.width(16)) r4 (.D(write_data), .en(and_4_out), .Q(r4_q), .clk(clk), .clr(1'b0));
  Register #(.width(16)) r5 (.D(write_data), .en(and_5_out), .Q(r5_q), .clk(clk), .clr(1'b0));
  Register #(.width(16)) r6 (.D(write_data), .en(and_6_out), .Q(r6_q), .clk(clk), .clr(1'b0));
  Register #(.width(16)) r7 (.D(write_data), .en(and_7_out), .Q(r7_q), .clk(clk), .clr(1'b0));
  Register #(.width(16)) r8 (.D(write_data), .en(and_8_out), .Q(r8_q), .clk(clk), .clr(1'b0));
  Multiplexer #(.select(3), .width(16), .disabled(0), .enable("false")) multiplexer_1 (
    .in0(r1_q), .in1(r2_q), .in2(r3_q), .in3(r4_q), .in4(r5_q), .in5(r6_q), .in6(r7_q), .in7(r8_q),
    .out(read_data_1), .sel(read_reg_1));
  Multiplexer #(.select(3), .width(16), .disabled(0), .enable("false")) multiplexer_2 (
    .in0(r1_q), .in1(r2_q), .in2(r3_q), .in3(r4_q), .in4(r5_q), .in5(r6_q), .in6(r7_q), .in7(r8_q),
    .out(read_data_2), .sel(read_reg_2));
endmodule

module ALU_control (
  input  [2:0] func,
  input  [2:0] ALUop,
  output [2:0] Operation
);

  or or_1 (Operation[1], func[1], ALUop[1]);
  or or_2 (Operation[0], func[0], ALUop[0]);
  or or_3 (Operation[2], func[2], ALUop[2]);
endmodule

module Control_Unit (
  input  [3:0] opcode,
  output jump,
  output RegDst,
  output halt,
  output branch,
  output RegWrite,
  output MemRead,
  output MemToReg,
  output zero,
  output aluSearch,
  output MemWrite,
  output [2:0] AluOP,
  output rtn,
  output min,
  output rightShift,
  output call
);

  wire and_1_out, and_4_out, and_5_out, and_8_out, and_9_out, and_10_out, and_11_out, and_12_out, and_15_out,
       nand_1_out, or_1_out;
  wire [2:0] multiplexer_1_out, multiplexer_2_out;

  and and_1 (and_1_out, ~opcode[3], ~opcode[2], ~opcode[1], ~opcode[0]);  // AND_Gate
  and and_2 (halt, opcode[3], opcode[2], opcode[1], opcode[0]);
  and and_3 (branch, ~opcode[3], opcode[2], ~opcode[1], ~opcode[0]);  // AND_Gate
  or or_1 (or_1_out, opcode[0], opcode[1]);
  and and_4 (and_4_out, ~opcode[3], opcode[2], ~opcode[1], opcode[0]);  // AND_Gate
  nand nand_1 (nand_1_out, opcode[1], opcode[0]);
  and and_5 (and_5_out, ~opcode[2], or_1_out, ~opcode[3]);  // AND_Gate
  and and_6 (MemWrite, opcode[3], ~opcode[2], opcode[1], opcode[0]);  // AND_Gate
  and and_7 (MemRead, opcode[3], ~opcode[2], ~opcode[1], opcode[0]);  // AND_Gate
  and and_8 (and_8_out, nand_1_out, and_5_out);
  and and_9 (and_9_out, nand_1_out, and_5_out);
  and and_10 (and_10_out, ~opcode[3], opcode[2], opcode[1], opcode[0]);  // AND_Gate
  and and_11 (and_11_out, and_8_out, opcode[0]);
  and and_12 (and_12_out, opcode[1], and_9_out);
  and and_13 (min, opcode[3], opcode[2], ~opcode[1], opcode[0]);  // AND_Gate
  and and_14 (rightShift, opcode[3], opcode[2], opcode[1], ~opcode[0]);  // AND_Gate
  and and_15 (and_15_out, opcode[3], opcode[2], ~opcode[1], ~opcode[0]);  // AND_Gate
  Multiplexer #(.width(3), .enable("false")) multiplexer_1 (
    .in0(3'b000), .in1(3'b000), .out(multiplexer_1_out), .sel(and_1_out));
  and and_16 (call, ~opcode[3], opcode[2], opcode[1], ~opcode[0]);  // AND_Gate
  Multiplexer #(.width(3), .enable("false")) multiplexer_2 (
    .in0(multiplexer_1_out), .in1(3'b011), .out(multiplexer_2_out), .sel(and_11_out));
  and and_17 (rtn, opcode[3], ~opcode[2], ~opcode[1], ~opcode[0]);  // AND_Gate
  or or_2 (zero, and_10_out, MemWrite, and_4_out);
  Multiplexer #(.width(3), .enable("false")) multiplexer_3 (
    .in0(multiplexer_2_out), .in1(3'b100), .out(AluOP), .sel(and_12_out));
  or or_3 (RegWrite, and_5_out, and_4_out, and_10_out, min, and_1_out, MemRead, rightShift);
  or or_4 (aluSearch, and_5_out, and_4_out);
  or or_5 (jump, and_15_out, call);
  or or_6 (RegDst, and_10_out, min, rightShift, and_1_out);

  assign MemToReg = MemRead;
endmodule

module Additional_ALU (
  input  [15:0] in_1,
  input  negative,
  input  [15:0] in_3,
  output [15:0] out_4
);

  wire [15:0] adder_1_out, subtractor_1_out;

  Adder #(.width(16)) adder_1 (.a(in_1), .b(in_3), .out(adder_1_out));  // open: cin, cout
  Subtractor #(.width(16)) subtractor_1 (.a(in_1), .b(in_3), .out(subtractor_1_out));  // open: bin, bout
  Multiplexer #(.width(16), .enable("false")) multiplexer_1 (
    .in0(adder_1_out), .in1(subtractor_1_out), .out(out_4), .sel(negative));
endmodule
